# Fritzing sketch goethe_pcb_v1 (saved by Fritzing 0.9.4)
breadboards: 1

parts:
  Part1 = Arduino Mega 2560 (Rev3)
  Mod1 = TMC2209 [package=THT]  # not connected
  Mod2 = TMC2209 [package=THT]
  Mod3 = TMC2209 [package=THT]
  Mod4 = TMC2209 [package=THT]  # not connected
  R1 = Resistor [tolerance=±5% resistance=1k package=THT]  # not connected
  R2 = Resistor [tolerance=±5% resistance=1k package=THT]  # not connected
  R3 = Resistor [tolerance=±5% resistance=1k package=THT]  # not connected
  R4 = Resistor [tolerance=±5% resistance=1k package=THT]  # not connected

nets:
  N1: Part1.5V, Mod2.EN
  N2: Mod3.GND, Mod3.VIO, Mod3.M2A, Mod3.M2B, Mod3.VM
  N3: Mod3.Dir, Mod3.Step
  N4: Mod3.SPRD, Mod3.MS1, Mod3.MS2, Mod3.EN

custom parts:
  TMC2209: TMC2209-LA stepper motor controller and driver. Supply voltage 4.75-28V Iphase up to 1.77A rms (2.5A peak)
